// Logisim project Controleur.circ as structural Verilog
module main (
  input  FLAG,
  input  [31:0] SortirFromCheminDeDonnes,
  output [3:0] Ra,
  output [3:0] Rb,
  output [3:0] Rd,
  output [3:0] CodeOp
);

  wire Clock_out;
  wire [7:0] adder_1_out, bitselector_1_out, multiplexer_1_out, undriven;
  wire [15:0] rom_1_data;

  ROM #(.dataWidth(16)) rom_1 (.addr(adder_1_out), .data(rom_1_data));
  Register #(.width(16)) RI (.D(rom_1_data));  // open: en, clk, Q, clr
  Clock Clock (.out(Clock_out));
  Multiplexer #(.width(8), .enable("false")) multiplexer_1 (
    .in0(bitselector_1_out), .in1(undriven), .out(multiplexer_1_out));  // open: sel
  Adder adder_1 (.a(multiplexer_1_out), .b(8'h4), .out(adder_1_out));  // open: cin, cout
  Register PC (.D(adder_1_out), .clk(Clock_out), .Q(adder_1_out));  // open: en, clr
  Controleur controleur_1 ();
  BitSelector #(.width(32), .group(8)) bitselector_1 (
    .in(SortirFromCheminDeDonnes), .out(bitselector_1_out), .sel(2'b11));

  // Notes on the sheet:
  //   contents of rom_1 (hex, n*v repeats v):
  //   1 10 11 100 101 110 111 1000 1001 1011 1100 1101 1100 1101 1110 1111
endmodule
